# Fritzing sketch Sleep_Wake_Interrupt_Arduino (saved by Fritzing 0.9.2b)
breadboards: 1

parts:
  Composant1 = Arduino Ethernet Shield (Rev3)
  LED1 = smd LED [color="Red (633nm)" package="0603 [SMD]"]
  S1 = Pushbutton [package="[THT]"]

nets:
  N1: Composant1.SPI/D13, LED1.anode
  N2: Composant1.D2, S1.Pin_3, S1.Pin_4
  N3: Composant1.GND, LED1.cathode, S1.Pin_1, S1.Pin_2
