# Fritzing sketch Water_Flow_Sensor (saved by Fritzing 0.9.2b)
circuit board: 8.46667cm x 5.64444cm
breadboards: 1

parts:
  LCD1 = LCD screen
  Composant1 = Arduino Nano (Rev3.0)
  R2 = Trimmer Potentiometer [maximum_resistance=10kΩ package=THT]
  S1 = Pushbutton [package="[SMD]"]
  J1 = Piezo Speaker
  LED1 = smd LED [color="Red (633nm)" package="0805 [SMD]"]

nets:
  VSS: LCD1.VSS, LCD1.R/W, LCD1.LED-, Composant1.GND, R2.leg2, S1.Pin_3, S1.Pin_4, J1.pin1, LED1.cathode
  VDD: LCD1.VDD, LCD1.LED+, Composant1.5V, R2.leg1
  N1: LCD1.V0, R2.wiper
  N2: LCD1.RS, Composant1.D12/MISO
  N3: LCD1.E, Composant1.D11/MOSI
  N4: LCD1.DB4, Composant1.D10
  N5: LCD1.DB5, Composant1.D9
  N6: LCD1.DB6, Composant1.D8
  N7: LCD1.DB7, Composant1.D7
  N8: Composant1.RESET, S1.Pin_1, S1.Pin_2
  N9: Composant1.D4, LED1.anode
  N10: Composant1.D5, J1.pin2
